# Fritzing sketch Beacon (saved by Fritzing 0.9.3b)
breadboards: 1

parts:
  U1 = atmega328 [package=dip]
  Q1 = TRANSISTOR_NPN [package=to-92-ammo]
  Code_0_-_1 = DIP SWITCH [package=dipswitch-02]
  Code_2_-_3 = DIP SWITCH [package=dipswitch-02]
  Time_and_Indication = DIP SWITCH [package=dipswitch-02]
  R1 = Resistor [tolerance=±5% resistance=10k package=THT]
  S1 = Pushbutton [package="[THT]"]
  XTAL1 = Crystal [frequency="16 Mhz" package=SMD]
  C1 = Ceramic Capacitor [capacitance=22pF voltage=6.3V package="100 mil [THT, multilayer]"]
  C2 = Ceramic Capacitor [capacitance=22pF voltage=6.3V package="100 mil [THT, multilayer]"]
  IR_1 = LEDs [package=led10mm]
  IR_2 = LEDs [package=led10mm]
  R2 = Resistor [tolerance=±5% resistance=33 package=THT]
  R3 = Resistor [tolerance=±5% resistance=33 package=THT]
  R4 = Resistor [tolerance=±5% resistance=10k package=THT]
  R5 = Resistor [tolerance=±5% resistance=10k package=THT]
  R6 = Resistor [tolerance=±5% resistance=10k package=THT]
  R7 = Resistor [tolerance=±5% resistance=10k package=THT]
  R8 = Resistor [tolerance=±5% resistance=10k package=THT]
  R9 = Resistor [tolerance=±5% resistance=10k package=THT]
  RGB_INDICATOR = RGB LED (com. anode, rbg) [package="5 mm [THT]"]
  R10 = Resistor [tolerance=±5% resistance=68 package=THT]
  R11 = Resistor [tolerance=±5% resistance=68 package=THT]
  R12 = Resistor [tolerance=±5% resistance=68 package=THT]

nets:
  N1: U1.RESET, R1.Pin_1, S1.Pin_3, S1.Pin_4
  N2: U1.D3_(PWM), Q1.B
  3V: U1.VCC, U1.AVCC, Code_0_-_1.1, Code_0_-_1.2, Code_2_-_3.1, Code_2_-_3.2, Time_and_Indication.1, Time_and_Indication.2, R1.Pin_0, RGB_INDICATOR.common_anode
  GND: U1.GND, Q1.E, S1.Pin_2, C1.0, C2.0, IR_1.C, IR_2.C, R4.Pin_1, R5.Pin_1, R6.Pin_1, R7.Pin_1, R8.Pin_1, R9.Pin_1
  N3: U1.XLAT1, XTAL1.pin_1, C1.1
  N4: U1.XLAT2, XTAL1.pin_0, C2.1
  N5: U1.D5_(PWM), R10.Pin_1
  N6: U1.D6_(PWM), R12.Pin_1
  N7: U1.D9_(PWM), R11.Pin_1
  N8: U1.D10_(PWM), Code_2_-_3.4, R7.Pin_0
  N9: U1.D11_(PWM), Code_2_-_3.3, R6.Pin_0
  N10: U1.D12, Code_0_-_1.4, R8.Pin_0
  N11: U1.D13, Code_0_-_1.3, R9.Pin_0
  N12: U1.A1, Time_and_Indication.4, R5.Pin_0
  N13: U1.A2, Time_and_Indication.3, R4.Pin_0
  N14: Q1.C, R2.Pin_1, R3.Pin_1
  N15: IR_1.A, R2.Pin_0
  N16: IR_2.A, R3.Pin_0
  N17: RGB_INDICATOR.red_cathode, R10.Pin_0
  N18: RGB_INDICATOR.blue_cathode, R11.Pin_0
  N19: RGB_INDICATOR.green_cathode, R12.Pin_0

notes:
  IR BEACON
